# Fritzing sketch sistema-midi-cyd-daisy-VEROBOARD-COMPLETO (saved by Fritzing 1.0.6)
breadboards: 2
stripboards: 1

parts:
  A1 = Arduino-midi-shield-through_1
  U1 = Daisy_Seed
  U3 = ESP32-2432S028R_1
  Power_plug1 = Power plug
  A2 = ESP32-S3-DevKitC-1 (dual USB)
  C1 = Electrolytic Capacitor [capacitance=0.1mF voltage=50V package="100 mil [THT, electrolytic]"]
  C2 = Electrolytic Capacitor [capacitance=0.1mF voltage=50V package="100 mil [THT, electrolytic]"]
  R1 = Resistor [resistance=10 power=0.25W tolerance=±5% package=THT]
  R2 = Resistor [resistance=10 power=0.25W tolerance=±5% package=THT]
  R3 = Resistor [resistance=10 power=0.25W tolerance=±5% package=THT]
  C4 = Electrolytic Capacitor [capacitance=0.1mF voltage=50V package="100 mil [THT, electrolytic]"]
  C5 = Electrolytic Capacitor [capacitance=0.1mF voltage=50V package="100 mil [THT, electrolytic]"]
  C6 = Electrolytic Capacitor [capacitance=0.1mF voltage=50V package="100 mil [THT, electrolytic]"]
  C7 = Electrolytic Capacitor [capacitance=0.1mF voltage=50V package="100 mil [THT, electrolytic]"]
  C8 = Ceramic Capacitor [capacitance=100nF voltage=50V package="100 mil [THT, multilayer]"]
  D1 = Schottky Diode [part_number=1N5817 package="300 mil [THT]"]
  C9 = Ceramic Capacitor [capacitance=100nF voltage=35V package="100 mil [THT, multilayer]"]
  C4_2 = Electrolytic Capacitor [capacitance=0.1mF voltage=50V package="100 mil [THT, electrolytic]"]
  C5_2 = Electrolytic Capacitor [capacitance=0.1mF voltage=50V package="100 mil [THT, electrolytic]"]
  C6_2 = Electrolytic Capacitor [capacitance=0.1mF voltage=50V package="100 mil [THT, electrolytic]"]
  C7_2 = Electrolytic Capacitor [capacitance=0.1mF voltage=50V package="100 mil [THT, electrolytic]"]
  C8_2 = Ceramic Capacitor [capacitance=100nF voltage=35V package="100 mil [THT, multilayer]"]

nets:
  N1: A1.connector2, Power_plug1.VCC, C8.1, D1.anode
  N2: A1.connector3, U3.connector8, Power_plug1.GND, C4.-, C5.-, C6.-, C7.-, C8.0
  N3: U1.connector7, A2.Pin_16
  N4: U1.connector8, A2.Pin_18
  N5: U1.connector9, A2.Pin_19
  N6: U1.connector10, A2.Pin_17
  N7: U1.connector19, U1.connector39, C1.-, C2.-, C9.1
  N8: U1.connector38, C2.+, R1.Pin_1, R2.Pin_1, R3.Pin_1, C9.0
  N9: U3.connector11, D1.cathode
  N10: A2.Pin_1, A2.Pin_2
  N11: A2.Pin_21, C1.+, R1.Pin_0, R2.Pin_0, R3.Pin_0, C4_2.+, C5_2.+, C6_2.+, C7_2.+, C8_2.1
  N12: A2.Pin_22, A2.Pin_23, A2.Pin_24, A2.Pin_44
  N13: C4.+, C5.+, C6.+, C7.+

custom parts:
  ESP32-S3-DevKitC-1 (dual USB): ESP32-S3 ESP32-S3-DevKitC-1 Dual USB development board Pyboard CircuitPython Micropython wifi BLE5.0 ESP32-S3. Based on a part by Werner Rothschopf, modified to ESP32-S3-DevKitC dual USB by vanepp, Aug 2024.
