# Fritzing sketch sistema-midi-cyd-daisy-VEROBOARD-FINAL-flipped - soldar (saved by Fritzing 1.0.6)
stripboards: 1

parts:
  A1 = Arduino-midi-shield-through_1
  U1 = Daisy_Seed
  U3 = ESP32-2432S028R_1
  A2 = ESP32-S3-DevKitC-1 (dual USB)
  switch_encendido_placas = Taiway 100-SP-X-T1 SPDT Miniature Toggle Switch [part_number=100-SP-X-T1-0-0-B1-M1 package=THT]
  U4 = 2.5mm Audio Jack [package=stereojack2.5mm_stereojack2.5mm]
  Squix1 = OLED 0.96" 128x64 I2C SSD1306
  Attack = POT [knob_status=50% power=0.5W package=alps_pot]
  swtich_filtro = Taiway 100-SP-X-T1 SPDT Miniature Toggle Switch [part_number=100-SP-X-T1-0-0-B1-M1 package=THT]
  Decay = POT [knob_status=50% power=0.5W package=alps_pot]
  Sustain = POT [knob_status=50% power=0.5W package=alps_pot]
  Release = POT [knob_status=50% power=0.5W package=alps_pot]
  Cutoff = POT [knob_status=50% power=0.5W package=alps_pot]
  Q = POT [knob_status=50% power=0.5W package=alps_pot]
  C15 = Ceramic Capacitor [capacitance=100nF voltage=35V package="100 mil [THT, multilayer]"]

nets:
  N1: A1.connector2, switch_encendido_placas.L1
  N2: A1.connector3, U1.connector19, U4.SLEEVE
  N3: A1.connector54, U1.connector14
  N4: U1.connector11, Squix1.SCL
  N5: U1.connector12, Squix1.SDA
  N6: U1.connector17, U4.LEFT
  N7: U1.connector18, U4.RIGHT
  N8: U1.connector20, Attack.E, swtich_filtro.L1, Decay.E, Sustain.E, Release.E, Cutoff.E, Q.E
  N9: U1.connector21, Attack.S
  N10: U1.connector22, Decay.S
  N11: U1.connector26, Q.S, C15.0
  N12: U1.connector28, swtich_filtro.COM
  N13: U1.connector29, Sustain.S
  N14: U1.connector30, Release.S
  N15: U1.connector31, Cutoff.S
  N16: U1.connector37, Squix1.VCC
  N17: U1.connector39, Squix1.GND, Attack.A, swtich_filtro.L2, Decay.A, Sustain.A, Release.A, Cutoff.A, Q.A
  N18: U3.connector1, A2.Pin_10
  N19: U3.connector2, A2.Pin_11
  N20: A2.Pin_1, A2.Pin_2
  N21: A2.Pin_22, A2.Pin_23, A2.Pin_24, A2.Pin_44

custom parts:
  ESP32-S3-DevKitC-1 (dual USB): ESP32-S3 ESP32-S3-DevKitC-1 Dual USB development board Pyboard CircuitPython Micropython wifi BLE5.0 ESP32-S3. Based on a part by Werner Rothschopf, modified to ESP32-S3-DevKitC dual USB by vanepp, Aug 2024.
