# Fritzing sketch sistema-midi-cyd-daisy-VEROBOARD-FINAL-v2 - copia (saved by Fritzing 1.0.6)
stripboards: 1

parts:
  A1 = Arduino-midi-shield-through_1
  U1 = Daisy_Seed
  U3 = ESP32-2432S028R_1
  Power_plug1 = Power plug
  A2 = ESP32-S3-DevKitC-1 (dual USB)
  C1 = Electrolytic Capacitor [capacitance=0.1mF voltage=50V package="100 mil [THT, electrolytic]"]
  C2 = Electrolytic Capacitor [capacitance=0.1mF voltage=50V package="100 mil [THT, electrolytic]"]
  R3 = Resistor [resistance=3.3 power=1W tolerance=±5% package=THT]
  C9 = Ceramic Capacitor [capacitance=100nF voltage=35V package="100 mil [THT, multilayer]"]
  C4 = Electrolytic Capacitor [capacitance=0.47mF voltage=50V package="100 mil [THT, electrolytic]"]
  C8 = Ceramic Capacitor [capacitance=100nF voltage=35V package="100 mil [THT, multilayer]"]
  switch_encendido_placas = Taiway 100-SP-X-T1 SPDT Miniature Toggle Switch [part_number=100-SP-X-T1-0-0-B1-M1 package=THT]
  D1 = Schottky Diode [part_number=1N5817 package="300 mil [THT]"]
  U4 = 2.5mm Audio Jack [package=stereojack2.5mm_stereojack2.5mm]
  Squix1 = OLED 0.96" 128x64 I2C SSD1306
  Attack = POT [knob_status=50% power=0.5W package=alps_pot]
  swtich_filtro = Taiway 100-SP-X-T1 SPDT Miniature Toggle Switch [part_number=100-SP-X-T1-0-0-B1-M1 package=THT]
  R4 = Resistor [tolerance=±5% power=0.25W resistance=10k package=THT]
  R5 = Resistor [tolerance=±5% power=0.25W resistance=10k package=THT]
  Decay = POT [knob_status=50% power=0.5W package=alps_pot]
  Sustain = POT [knob_status=50% power=0.5W package=alps_pot]
  Release = POT [knob_status=50% power=0.5W package=alps_pot]
  Cutoff = POT [knob_status=50% power=0.5W package=alps_pot]
  Q = POT [knob_status=50% power=0.5W package=alps_pot]
  C10 = Ceramic Capacitor [capacitance=100nF voltage=35V package="100 mil [THT, multilayer]"]
  C11 = Ceramic Capacitor [capacitance=100nF voltage=35V package="100 mil [THT, multilayer]"]
  C12 = Ceramic Capacitor [capacitance=100nF voltage=35V package="100 mil [THT, multilayer]"]
  C13 = Ceramic Capacitor [capacitance=100nF voltage=35V package="100 mil [THT, multilayer]"]
  C14 = Ceramic Capacitor [capacitance=100nF voltage=35V package="100 mil [THT, multilayer]"]
  C15 = Ceramic Capacitor [capacitance=100nF voltage=35V package="100 mil [THT, multilayer]"]

nets:
  N1: A1.connector2, A2.Pin_21, C1.+, R3.Pin_0, switch_encendido_placas.L2, D1.anode
  GND: A1.connector3, U1.connector19, U1.connector39, U3.connector0, U3.connector8, Power_plug1.GND, A2.Pin_22, A2.Pin_23, A2.Pin_24, A2.Pin_44, C1.-, C2.-, C9.1, C4.-, C8.1, U4.SLEEVE, Squix1.GND, Attack.A, swtich_filtro.L2, R5.Pin_1, Decay.A, Sustain.A, Release.A, Cutoff.A, Q.A, C10.1, C11.1, C12.1, C13.1, C14.1, C15.1
  N2: A1.connector54, U1.connector14
  N3: U1.connector7, A2.Pin_16
  N4: U1.connector8, A2.Pin_18
  N5: U1.connector9, A2.Pin_19
  N6: U1.connector10, A2.Pin_17
  N7: U1.connector11, Squix1.SCL
  N8: U1.connector12, Squix1.SDA
  N9: U1.connector17, U4.LEFT
  N10: U1.connector18, U4.RIGHT
  N11: U1.connector20, Attack.E, swtich_filtro.L1, R4.Pin_0, Decay.E, Sustain.E, Release.E, Cutoff.E, Q.E
  N12: U1.connector21, Attack.S, C10.0
  N13: U1.connector22, Decay.S, C11.0
  N14: U1.connector23, Sustain.S, C12.0
  N15: U1.connector24, Release.S, C13.0
  N16: U1.connector25, Cutoff.S, C14.0
  N17: U1.connector26, Q.S, C15.0
  N18: U1.connector27, swtich_filtro.COM, R4.Pin_1, R5.Pin_0
  N19: U1.connector37, Squix1.VCC
  N20: U1.connector38, C2.+, R3.Pin_1, C9.0
  N21: U3.connector1, A2.Pin_10
  N22: U3.connector2, A2.Pin_11
  N23: U3.connector11, D1.cathode
  N24: Power_plug1.VCC, C4.+, C8.0, switch_encendido_placas.COM
  N25: A2.Pin_1, A2.Pin_2

custom parts:
  ESP32-S3-DevKitC-1 (dual USB): ESP32-S3 ESP32-S3-DevKitC-1 Dual USB development board Pyboard CircuitPython Micropython wifi BLE5.0 ESP32-S3. Based on a part by Werner Rothschopf, modified to ESP32-S3-DevKitC dual USB by vanepp, Aug 2024.
