# Fritzing sketch sistema-midi-cyd-daisy-VEROBOARD-FINAL (saved by Fritzing 1.0.6)
breadboards: 2
stripboards: 1

parts:
  A1 = Arduino-midi-shield-through_1
  U1 = Daisy_Seed
  U3 = ESP32-2432S028R_1
  Power_plug1 = Power plug
  A2 = ESP32-S3-DevKitC-1 (dual USB)
  C1 = Electrolytic Capacitor [capacitance=0.1mF voltage=50V package="100 mil [THT, electrolytic]"]
  C2 = Electrolytic Capacitor [capacitance=0.1mF voltage=50V package="100 mil [THT, electrolytic]"]
  R1 = Resistor [resistance=10 power=0.25W tolerance=±5% package=THT]
  R2 = Resistor [resistance=10 power=0.25W tolerance=±5% package=THT]
  R3 = Resistor [resistance=10 power=0.25W tolerance=±5% package=THT]
  C4 = Electrolytic Capacitor [capacitance=0.1mF voltage=50V package="100 mil [THT, electrolytic]"]
  C5 = Electrolytic Capacitor [capacitance=0.1mF voltage=50V package="100 mil [THT, electrolytic]"]
  C6 = Electrolytic Capacitor [capacitance=0.1mF voltage=50V package="100 mil [THT, electrolytic]"]
  C7 = Electrolytic Capacitor [capacitance=0.1mF voltage=50V package="100 mil [THT, electrolytic]"]
  C8 = Ceramic Capacitor [capacitance=100nF voltage=50V package="100 mil [THT, multilayer]"]
  D1 = Schottky Diode [part_number=1N5817 package="300 mil [THT]"]
  C9 = Ceramic Capacitor [capacitance=100nF voltage=35V package="100 mil [THT, multilayer]"]
  C4_2 = Electrolytic Capacitor [capacitance=0.1mF voltage=50V package="100 mil [THT, electrolytic]"]
  C5_2 = Electrolytic Capacitor [capacitance=0.1mF voltage=50V package="100 mil [THT, electrolytic]"]
  C6_2 = Electrolytic Capacitor [capacitance=0.1mF voltage=50V package="100 mil [THT, electrolytic]"]
  C7_2 = Electrolytic Capacitor [capacitance=0.1mF voltage=50V package="100 mil [THT, electrolytic]"]
  C8_2 = Ceramic Capacitor [capacitance=100nF voltage=35V package="100 mil [THT, multilayer]"]
  POT_A = Rotary Potentiometer (Small) [package=THT]
  POT_D = Rotary Potentiometer (Small) [package=THT]
  POT_S = Rotary Potentiometer (Small) [package=THT]
  POT_R = Rotary Potentiometer (Small) [package=THT]
  POT_CUT = Rotary Potentiometer (Small) [package=THT]
  POT_Q = Rotary Potentiometer (Small) [package=THT]
  SELECTOR_filtro_(3_pos_LPF/HPF/BPF) = Taiway 100-SP-X-T1 SPDT Miniature Toggle Switch [package=THT]
  OLED_0_96_I2C = Grove OLED 128x96
  JACK_3_5mm_salida_audio = Audio Jack Breakout

nets:
  N1: A1.connector2, U3.connector11, Power_plug1.VCC, A2.Pin_21, C1.+, R1.Pin_0, R2.Pin_0, R3.Pin_0, C8.1, D1.cathode, D1.anode, C4_2.+, C5_2.+, C6_2.+, C7_2.+, C8_2.1
  N2: A1.connector3, U3.connector8, Power_plug1.GND, C4.-, C5.-, C6.-, C7.-, C8.0
  N3: A1.connector54, U1.connector14
  N4: U1.connector7, A2.Pin_16
  N5: U1.connector8, A2.Pin_18
  N6: U1.connector9, A2.Pin_19
  N7: U1.connector10, A2.Pin_17
  N8: U1.connector11, OLED_0_96_I2C.SCL
  N9: U1.connector12, OLED_0_96_I2C.SDA
  N10: U1.connector17, JACK_3_5mm_salida_audio.TIP
  GND: U1.connector19, U1.connector39, C1.-, C2.-, C9.1, POT_A.leg2, POT_D.leg2, POT_S.leg2, POT_R.leg2, POT_CUT.leg2, POT_Q.leg2, SELECTOR_filtro_(3_pos_LPF/HPF/BPF).L2, OLED_0_96_I2C.GND, JACK_3_5mm_salida_audio.GND
  N11: U1.connector20, POT_A.leg1, POT_D.leg1, POT_S.leg1, POT_R.leg1, POT_CUT.leg1, POT_Q.leg1, SELECTOR_filtro_(3_pos_LPF/HPF/BPF).L1
  N12: U1.connector21, POT_A.wiper
  N13: U1.connector22, POT_D.wiper
  N14: U1.connector23, POT_S.wiper
  N15: U1.connector24, POT_R.wiper
  N16: U1.connector25, POT_CUT.wiper
  N17: U1.connector26, POT_Q.wiper
  N18: U1.connector27, SELECTOR_filtro_(3_pos_LPF/HPF/BPF).COM
  N19: U1.connector37, OLED_0_96_I2C.VCC
  N20: U1.connector38, C2.+, R1.Pin_1, R2.Pin_1, R3.Pin_1, C9.0
  N21: U3.connector5, A2.Pin_11
  N22: A2.Pin_1, A2.Pin_2
  N23: A2.Pin_22, A2.Pin_23, A2.Pin_24, A2.Pin_44
  N24: C4.+, C5.+, C6.+, C7.+

custom parts:
  ESP32-S3-DevKitC-1 (dual USB): ESP32-S3 ESP32-S3-DevKitC-1 Dual USB development board Pyboard CircuitPython Micropython wifi BLE5.0 ESP32-S3. Based on a part by Werner Rothschopf, modified to ESP32-S3-DevKitC dual USB by vanepp, Aug 2024.
