# Fritzing sketch sistema-midi-cyd-daisy.BACKUP (saved by Fritzing 1.0.6)
breadboards: 2

parts:
  A1 = Arduino-midi-shield-through_1
  U1 = Daisy_Seed
  U3 = ESP32-2432S028R_1
  Power_plug1 = Power plug
  A2 = ESP32-S3-DevKitC-1 (dual USB)
  C1 = Electrolytic Capacitor [capacitance=0.1mF voltage=20V package="100 mil [THT, electrolytic]"]
  R1 = Resistor [tolerance=±5% power=0.25W resistance=3.3 package=THT]
  C2 = Electrolytic Capacitor [capacitance=0.1mF voltage=20V package="100 mil [THT, electrolytic]"]
  R2 = Resistor [tolerance=±5% power=0.25W resistance=3.3 package=THT]
  C3 = Electrolytic Capacitor [capacitance=0.1mF voltage=35V package="100 mil [THT, electrolytic]"]

nets:
  N1: A1.connector2, U1.connector38, U3.connector11, A2.Pin_21, R2.Pin_0, C3.+
  N2: A1.connector3, U1.connector19, U1.connector39, U3.connector8, Power_plug1.GND, A2.Pin_22, A2.Pin_23, A2.Pin_24, A2.Pin_44, C1.-, C2.-, C3.-
  N3: A1.connector54, U1.connector14
  N4: U1.connector7, A2.Pin_16
  N5: U1.connector8, A2.Pin_18
  N6: U1.connector9, A2.Pin_19
  N7: U1.connector10, A2.Pin_17
  N8: U3.connector5, A2.Pin_11
  N9: Power_plug1.VCC, R1.Pin_1, C2.+
  N10: A2.Pin_1, A2.Pin_2
  N11: C1.+, R1.Pin_0, R2.Pin_1

custom parts:
  ESP32-S3-DevKitC-1 (dual USB): ESP32-S3 ESP32-S3-DevKitC-1 Dual USB development board Pyboard CircuitPython Micropython wifi BLE5.0 ESP32-S3. Based on a part by Werner Rothschopf, modified to ESP32-S3-DevKitC dual USB by vanepp, Aug 2024.
