# Fritzing sketch sistema-midi-cyd-daisy (saved by Fritzing 1.0.6)
breadboards: 2

parts:
  A1 = Arduino-midi-shield-through_1
  U1 = Daisy_Seed
  U3 = ESP32-2432S028R_1
  Power_plug1 = Power plug
  A2 = ESP32-S3-DevKitC-1 (dual USB)
  C1 = Electrolytic Capacitor [capacitance=0.1mF voltage=50V package="100 mil [THT, electrolytic]"]
  C2 = Electrolytic Capacitor [capacitance=0.1mF voltage=50V package="100 mil [THT, electrolytic]"]
  R1 = Resistor [resistance=10 power=0.25W tolerance=±5% package=THT]
  R2 = Resistor [resistance=10 power=0.25W tolerance=±5% package=THT]
  R3 = Resistor [resistance=10 power=0.25W tolerance=±5% package=THT]
  C4 = Electrolytic Capacitor [capacitance=0.1mF voltage=50V package="100 mil [THT, electrolytic]"]
  C5 = Electrolytic Capacitor [capacitance=0.1mF voltage=50V package="100 mil [THT, electrolytic]"]
  C6 = Electrolytic Capacitor [capacitance=0.1mF voltage=50V package="100 mil [THT, electrolytic]"]
  C7 = Electrolytic Capacitor [capacitance=0.1mF voltage=50V package="100 mil [THT, electrolytic]"]
  C8 = Ceramic Capacitor [capacitance=100nF voltage=50V package="100 mil [THT, multilayer]"]
  D1 = Schottky Diode [part_number=1N5817 package="300 mil [THT]"]

nets:
  N1: A1.connector2, Power_plug1.VCC, C1.+, R1.Pin_0, R2.Pin_0, R3.Pin_0, C8.1, D1.anode
  N2: A1.connector3, U1.connector19, U1.connector39, U3.connector8, Power_plug1.GND, C1.-, C2.-, C4.-, C5.-, C6.-, C7.-, C8.0
  N3: A1.connector54, U1.connector14
  N4: U1.connector38, C2.+, R1.Pin_1, R2.Pin_1, R3.Pin_1
  N5: U3.connector11, D1.cathode
  N6: A2.Pin_23, A2.Pin_24, A2.Pin_44
  N7: C4.+, C5.+, C6.+, C7.+

custom parts:
  ESP32-S3-DevKitC-1 (dual USB): ESP32-S3 ESP32-S3-DevKitC-1 Dual USB development board Pyboard CircuitPython Micropython wifi BLE5.0 ESP32-S3. Based on a part by Werner Rothschopf, modified to ESP32-S3-DevKitC dual USB by vanepp, Aug 2024.
